// Logisim project ALU.circ as structural Verilog
module ALU (
  input  [7:0] R1__Value_of_first_register,
  input  [7:0] R2__Value_of_second_register,
  input  [3:0] COM__Value_of_command__0000_to_1111,
  output [7:0] OUT__ALU_output,
  output FL__output_to_FLAG
);

  wire sabirac_1_of, subtractor_1_of;
  wire [7:0] and_1_out, not_1_out, or_1_out, rol_1_out_3, ror_1_out_3, sabirac_1_out_3, shl_1_out_3,
       shr_1_out_3, subtractor_1_z;

  Sabirac sabirac_1 (
    .X(R1__Value_of_first_register), .Y(R2__Value_of_second_register), .out_3(sabirac_1_out_3),
    .OF(sabirac_1_of));
  Subtractor subtractor_1 (
    .X(R1__Value_of_first_register), .Y(R2__Value_of_second_register), .Z(subtractor_1_z),
    .OF(subtractor_1_of));
  SHL shl_1 (.in_1(R1__Value_of_first_register), .X(R2__Value_of_second_register), .out_3(shl_1_out_3));
  SHR shr_1 (.in_1(R1__Value_of_first_register), .X(R2__Value_of_second_register), .out_3(shr_1_out_3));
  ROL rol_1 (.in_1(R1__Value_of_first_register), .X(R2__Value_of_second_register), .out_3(rol_1_out_3));
  ROR ror_1 (.in_1(R1__Value_of_first_register), .X(R2__Value_of_second_register), .out_3(ror_1_out_3));
  assign not_1_out = ~R1__Value_of_first_register;  // NOT_Gate not_1, 8 bits wide
  assign and_1_out = R1__Value_of_first_register & R2__Value_of_second_register;  // AND_Gate and_1, 8 bits wide
  assign or_1_out = R2__Value_of_second_register | R1__Value_of_first_register;  // OR_Gate or_1, 8 bits wide
  Multiplexer #(.select(4), .width(8)) multiplexer_1 (
    .in0(R1__Value_of_first_register), .in1(R1__Value_of_first_register), .in2(R1__Value_of_first_register),
    .in3(sabirac_1_out_3), .in4(subtractor_1_z), .in5({8{1'b0}}), .in6(R1__Value_of_first_register),
    .in7(shl_1_out_3), .in8(shr_1_out_3), .in9(rol_1_out_3), .in10(ror_1_out_3), .in11(not_1_out),
    .in12(and_1_out), .in13(or_1_out), .in14({8{1'b1}}), .in15({8{1'b1}}), .out(OUT__ALU_output),
    .sel(COM__Value_of_command__0000_to_1111));  // open: en
  or or_2 (FL__output_to_FLAG, sabirac_1_of, subtractor_1_of);
endmodule

// FIlter Flags
module flag_filters (
  input  OF,
  input  [7:0] ALU_output,
  output [3:0] ZCOP
);

  wire [7:0] not_2_out;

  not not_1 (ZCOP[0], not_2_out[0]);
  assign not_2_out = ~ALU_output;  // NOT_Gate not_2, 8 bits wide
  and and_1 (ZCOP[3], not_2_out[7], not_2_out[6], not_2_out[5], not_2_out[4], not_2_out[3], not_2_out[2], not_2_out[1], not_2_out[0]);

  assign ZCOP[2:1] = {2{OF}};
endmodule
