// Logisim project BOB-CPU.circ as structural Verilog: 1 circuit, main circuit BOB
module BOB (
  output [3:0] ZCOP,
  output [7:0] out_2,
  output [7:0] out_3
);

  wire CLK_out, cu_1_p2, cu_1_p3, cu_1_p4, cu_1_p6, cu_1_p7, cu_1_p8, cu_1_p9, not_1_out, not_2_out,
       not_3_out;
  wire [3:0] cu_1_p10, flags_1_p1;
  wire [7:0] cu_1_p5, pc_1_cl__current_line, ram_2_data, registers_1_p11, registers_1_p12;
  wire [15:0] cu_1_p1;

  Clock CLK (.out(CLK_out));
  PC pc_1 (
    .CLK(CLK_out), .CL__current_line(pc_1_cl__current_line), .JMP__Input_for_JMP_command(out_2),
    .CJ__if_1__JMP_is_allowed(ZCOP[3]), .J__if_1__JMP_is_allowed(cu_1_p2));
  not not_1 (not_1_out, 1'b1);
  // CU cu_1: pin names not known; wires that end beside it: cu_1_p1, cu_1_p2, cu_1_p3, cu_1_p4, cu_1_p5, cu_1_p6, cu_1_p7, cu_1_p8, cu_1_p9, cu_1_p10
  RAM #(.dataWidth(16), .bus("separate")) ram_1 (
    .addr(pc_1_cl__current_line), .data(cu_1_p1), .str(not_1_out), .clk(CLK_out), .ld(1'b1));  // open: din, sel, clr
  not not_2 (not_2_out, cu_1_p4);
  RAM #(.bus("separate")) ram_2 (
    .addr(cu_1_p5), .din(out_3), .data(ram_2_data), .str(cu_1_p4), .clk(CLK_out), .ld(not_2_out));  // open: sel, clr
  not not_3 (not_3_out, cu_1_p4);
  // Registers registers_1: pin names not known; wires that end beside it: out_2, ram_2_data, cu_1_p7, cu_1_p8, cu_1_p9, CLK_out, cu_1_p6, cu_1_p3, not_3_out, out_3, registers_1_p11, registers_1_p12
  // Flags flags_1: pin names not known; wires that end beside it: flags_1_p1, CLK_out, ZCOP[0], ZCOP[1], ZCOP[2], ZCOP[3]
  ALU alu_1 (
    .R1__Value_of_first_register(registers_1_p11), .R2__Value_of_second_register(registers_1_p12),
    .OUT__ALU_output(out_2), .COM__Value_of_command__0000_to_1111(cu_1_p10), .FLAGS_ZCOP(flags_1_p1));
endmodule
