// Logisim project procesor.circ as structural Verilog
module Procesor (
  input  [15:0] I_Input,
  input  LD,
  input  [15:0] in_3,
  output [15:0] I_Output,
  output [7:0] ALU_Output,
  output [7:0] out_6,
  output [2:0] out_7
);

  wire CLK_out, main_1_p3, main_1_p4, main_1_p5, main_1_p7, main_1_p8, not_1_out;
  wire [3:0] main_1_p6;
  wire [7:0] MEM, multiplexer_1_out, ram_2_data, registers_1_p9, registers_1_p10;

  Clock CLK (.out(CLK_out));
  Multiplexer #(.width(8)) multiplexer_1 (
    .in0(ALU_Output), .in1(ram_2_data), .out(multiplexer_1_out), .sel(main_1_p5));  // open: en
  // CU_main main_1: pin names not known; wires that end beside it: in_3, MEM, main_1_p3, main_1_p4, main_1_p5, main_1_p6, main_1_p7, main_1_p8, out_7
  not not_1 (not_1_out, main_1_p4);
  RAM #(.dataWidth(16), .bus("separate")) ram_1 (
    .din(I_Input), .data(I_Output), .clk(CLK_out), .ld(LD));  // open: addr, str, sel, clr
  // Registers registers_1: pin names not known; wires that end beside it: multiplexer_1_out, main_1_p7, main_1_p8, out_7, CLK_out, main_1_p3, not_1_out, out_6, registers_1_p9, registers_1_p10
  RAM #(.bus("separate")) ram_2 (
    .addr(MEM), .din(out_6), .data(ram_2_data), .str(main_1_p4), .clk(CLK_out), .ld(not_1_out));  // open: sel, clr
  ALU alu_1 (
    .R1__Value_of_first_register(registers_1_p9), .R2__Value_of_second_register(registers_1_p10),
    .OUT__ALU_output(ALU_Output), .COM__Value_of_command__0000_to_1111(main_1_p6));  // open: FL__output_to_FLAG

  // Other names for the same wires on the sheet: AX[7:0] = out_6

  // Notes on the sheet:
  //   Instruction
  //   Memory Adress
  //   1
  //   INSTRUCTIONS
  //   5,6,7
  //   DATA
  //   2
  //   3
  //   3
  //   4
  //   ALU_Value
  //   3. Value of first adress 
  //   4. Value of second adress
  //   5. First adress
  //   6. Second adress
  //   7. Input adress
  //   1. bit(value = is this instruction MOV)
  //   2. bit(value = is this instruction LOAD or STORE)
endmodule
